// Logisim project alu.circ as structural Verilog: 1 circuit, main circuit main
module main (
  input  [5:0] Switch__S,
  input  [31:0] X,
  input  [31:0] Y,
  output Signed_Overflow,
  output [31:0] RESULT,
  output Equal
);

  wire adder_2_cout, adder_3_cout, comparator_1_lt, comparator_2_lt, comparator_4_eq, overflow_add,
       overflow_sub, subtractor_2_bout, subtractor_3_bout;
  wire [4:0] bit_extender_1_out, bit_extender_2_out, bit_extender_3_out;
  wire [5:0] adder_4_out, bitadder_1_out, bitadder_2_out;
  wire [31:0] add, addu, \and , bitpal, cnto, \or , sll, slt, sltu, sra, srl, sub, subu;

  Shifter #(.width(32)) shifter_1 (.in(X), .\dist (bit_extender_1_out), .out(sll));
  Bit_Extender #(.in_width(32), .out_width(5)) bit_extender_1 (.in(Y), .out(bit_extender_1_out));
  Shifter #(.width(32), .shift("lr")) shifter_2 (.in(X), .\dist (bit_extender_2_out), .out(srl));
  Bit_Extender #(.in_width(32), .out_width(5)) bit_extender_2 (.in(Y), .out(bit_extender_2_out));
  Shifter #(.width(32), .shift("ar")) shifter_3 (.in(X), .\dist (bit_extender_3_out), .out(sra));
  Bit_Extender #(.in_width(32), .out_width(5)) bit_extender_3 (.in(Y), .out(bit_extender_3_out));
  assign \and  = X & Y;  // AND_Gate AND, 32 bits wide
  assign \or  = X | Y;  // OR_Gate OR, 32 bits wide
  Adder #(.width(32)) adder_1 (.a(X), .b(Y), .out(addu));  // open: cin, cout
  Subtractor #(.width(32)) subtractor_1 (.a(X), .b(Y), .out(subu));  // open: bin, bout
  Comparator #(.width(32)) comparator_1 (.a(X), .b(Y), .lt(comparator_1_lt));  // open: gt, eq
  assign slt = {{31{1'b0}}, comparator_1_lt};  // Bit_Extender bit_extender_4
  Comparator #(.width(32), .mode("unsigned")) comparator_2 (.a(X), .b(Y), .lt(comparator_2_lt));  // open: gt, eq
  assign sltu = {{31{1'b0}}, comparator_2_lt};  // Bit_Extender bit_extender_5
  Comparator #(.width(32), .mode("unsigned")) comparator_3 (.a(X), .b(Y), .eq(Equal));  // open: gt, lt
  BitAdder #(.width(32)) bitadder_1 (.in0(X), .out(bitadder_1_out));
  BitAdder #(.width(32)) bitadder_2 (.in0(Y), .out(bitadder_2_out));
  Multiplexer #(.select(5), .width(32)) multiplexer_1 (
    .in0(sll), .in2(srl), .in3(sra), .in16(add), .in17(addu), .in18(sub), .in19(subu), .in20(\and ),
    .in21(\or ), .in26(slt), .in27(sltu), .in28(cnto), .in30(bitpal), .out(RESULT),
    .sel({Switch__S[5], Switch__S[3:0]}));  // open: in1, in4, in5, in6, in7, in8, in9, in10, in11, in12, in13, in14, in15, in22, in23, in24, in25, in29, in31, en
  Comparator #(.width(16), .mode("unsigned")) comparator_4 (
    .a({X[0], X[1], X[2], X[3], X[4], X[5], X[6], X[7], X[8], X[9], X[10], X[11], X[12], X[13], X[14], X[15]}),
    .b(X[31:16]), .eq(comparator_4_eq));  // open: gt, lt
  Multiplexer #(.select(5), .enable("false")) multiplexer_2 (
    .in0(1'b0), .in2(1'b0), .in3(1'b0), .in16(overflow_add), .in17(1'b0), .in18(overflow_sub), .in19(1'b0),
    .in20(1'b0), .in21(1'b0), .in25(1'b0), .in26(1'b0), .in27(1'b0), .in28(1'b0), .in30(1'b0),
    .out(Signed_Overflow), .sel({Switch__S[5], Switch__S[3:0]}));  // open: in1, in4, in5, in6, in7, in8, in9, in10, in11, in12, in13, in14, in15, in22, in23, in24, in29, in31
  Adder #(.width(31)) adder_2 (.a(X[30:0]), .b(Y[30:0]), .out(add[30:0]), .cout(adder_2_cout));  // open: cin
  Adder #(.width(1)) adder_3 (.a(Y[31]), .b(X[31]), .out(add[31]), .cin(adder_2_cout), .cout(adder_3_cout));
  Subtractor #(.width(31)) subtractor_2 (
    .a(X[30:0]), .b(Y[30:0]), .out(sub[30:0]), .bout(subtractor_2_bout));  // open: bin
  Subtractor #(.width(1)) subtractor_3 (
    .a(X[31]), .b(Y[31]), .out(sub[31]), .bin(subtractor_2_bout), .bout(subtractor_3_bout));
  assign bitpal = {{31{1'b0}}, comparator_4_eq};  // Bit_Extender bit_extender_6
  Adder #(.width(6)) adder_4 (.a(bitadder_1_out), .b(bitadder_2_out), .out(adder_4_out));  // open: cin, cout
  assign cnto = {{26{1'b0}}, adder_4_out};  // Bit_Extender bit_extender_7
  xor xor_1 (overflow_add, adder_2_cout, adder_3_cout);
  xor xor_2 (overflow_sub, subtractor_2_bout, subtractor_3_bout);

  // Other names for the same wires on the sheet: Input_X[31:0] = X; Input_Y[31:0] = Y

  // Notes on the sheet:
  //   INPUT to your circuit
  //   INPUTS to your circuit
  //   DON'T CHANGE THE INPUTS AND OUTPUTS! IF YOU DO SO, YOU NEED TO MAKE SURE THE PINS ARE IN THE RIGHT PLACES!
  //   OUTPUTS of your circuit
endmodule
