// Logisim project cpu.circ as structural Verilog: 2 circuits, main circuit main
module main (
  input  [31:0] RS_READ_VALUE,
  input  [31:0] RT_READ_VALUE,
  input  [31:0] INSTRUCTION,
  input  CLOCK,
  input  RESET,
  output [31:0] t0,
  output [31:0] t1,
  output [31:0] t2,
  output [31:0] t3,
  output [4:0] RT,
  output [4:0] RS,
  output [4:0] Write_Register,
  output [31:0] RD_WRITE_VALUE,
  output RD_WRITE_ENABLE,
  output [23:0] FETCH_ADDRESS
);

  wire accessByte, ALU_signed_overflow, aluEq, aluSrc, and_1_out, and_2_out, and_3_out, and_4_out, beq, bne,
       comparator_1_lt, comparator_2_lt, comparator_3_eq, comparator_4_lt, comparator_5_lt, comparator_6_lt,
       comparator_7_lt, isBranchTaken, jal, jr, jump, kill, lui, memToReg, memWr, not_1_out, regDest, rsTmp,
       rtTmp, shamt_t, zeroExt;
  wire [1:0] multiplexer_2_out;
  wire [4:0] wrReg;
  wire [5:0] aluCtrl;
  wire [7:0] bit_extender_1_out;
  wire [15:0] ADDRESS_J_t;
  wire [23:0] adder_1_out, adder_2_out, adder_3_out, ADDRESS_J, bit_extender_2_out, branchVal,
       multiplexer_3_out, multiplexer_16_out, nextPC, subtractor_2_out, subtractor_3_out;
  wire [31:0] ALU_result, bit_extender_3_out, bit_extender_4_out, bit_extender_5_out, bit_extender_6_out,
       bit_extender_7_out, MEM_data_mem_out, multiplexer_5_out, multiplexer_7_out, multiplexer_11_out,
       multiplexer_13_out, multiplexer_14_out, multiplexer_15_out, RegFile_read_data_1, RegFile_read_data_2,
       rt_dataIn, subtractor_1_out, valueForBranch, wrData, X, Y;
  wire [31:26] INSTRUCTION_t;

  Register #(.width(24)) PC (.D(nextPC), .Q(FETCH_ADDRESS), .clk(CLOCK));  // open: en, clr
  alu_main ALU (
    .X(X), .RESULT(ALU_result), .Signed_Overflow(ALU_signed_overflow), .Y(Y), .Switch__S(aluCtrl));  // open: Equal
  and and_1 (and_1_out, bne, not_1_out);
  not not_1 (not_1_out, aluEq);
  Multiplexer #(.width(5)) multiplexer_1 (.in0(RT), .in1(ADDRESS_J_t[15:11]), .out(wrReg), .sel(regDest));  // open: en
  LED led_1 (.in(ALU_signed_overflow));
  and and_2 (and_2_out, aluEq, beq);
  Multiplexer #(.width(2)) multiplexer_2 (
    .in0(RT[1:0]), .in1(ADDRESS_J_t[12:11]), .out(multiplexer_2_out), .sel(regDest));  // open: en
  mem_main MEM (
    .Data_Mem_Addr(ALU_result), .Data_Mem_In(rt_dataIn), .ACCESS_BYTE(accessByte), .CLOCK(memWr),
    .MEM_WRITE(CLOCK), .Data_Mem_Out(MEM_data_mem_out));
  or or_1 (isBranchTaken, and_1_out, and_2_out);
  regfile_main RegFile (
    .Read_register_1(RS[1:0]), .Read_register_2(RT[1:0]), .write_register(multiplexer_2_out),
    .write_data(wrData), .t0_Value(t0), .t1_Value(t1), .t2_Value(t2), .t3_Value(t3), .clock(CLOCK),
    .RegWrite(and_4_out), .Read_Data_1(RegFile_read_data_1), .Read_Data_2(RegFile_read_data_2));
  Comparator #(.width(5), .mode("unsigned")) comparator_1 (
    .a(5'b00111), .b(wrReg), .lt(comparator_1_lt));  // open: gt, eq
  Comparator #(.width(5), .mode("unsigned")) comparator_2 (
    .a(wrReg), .b(5'b01100), .lt(comparator_2_lt));  // open: gt, eq
  Bit_Extender #(.in_width(32), .out_width(8)) bit_extender_1 (.in(MEM_data_mem_out), .out(bit_extender_1_out));
  Adder #(.width(24)) adder_1 (.a(FETCH_ADDRESS), .b(24'h1), .out(adder_1_out));  // open: cin, cout
  Multiplexer #(.width(24)) multiplexer_3 (
    .in0(adder_1_out), .in1(FETCH_ADDRESS), .out(multiplexer_3_out), .sel(kill));  // open: en
  assign bit_extender_2_out = {{8{ADDRESS_J_t[15]}}, ADDRESS_J_t};  // Bit_Extender bit_extender_2
  and and_3 (and_3_out, comparator_1_lt, comparator_2_lt);
  assign bit_extender_3_out = {{24{bit_extender_1_out[7]}}, bit_extender_1_out};  // Bit_Extender bit_extender_3
  Comparator #(.width(6)) comparator_3 (.a(INSTRUCTION_t), .b(6'b100000), .eq(comparator_3_eq));  // open: gt, lt
  Multiplexer #(.width(24)) multiplexer_4 (
    .in0(multiplexer_3_out), .in1(adder_2_out), .out(branchVal), .sel(isBranchTaken));  // open: en
  Adder #(.width(24)) adder_2 (.a(multiplexer_3_out), .b(bit_extender_2_out), .out(adder_2_out));  // open: cin, cout
  Multiplexer #(.width(32)) multiplexer_5 (
    .in0(INSTRUCTION), .in1({32{1'b0}}), .out(multiplexer_5_out), .sel(kill));  // open: en
  and and_4 (and_4_out, RD_WRITE_ENABLE, and_3_out);
  Multiplexer #(.width(32)) multiplexer_6 (
    .in0(ALU_result), .in1(multiplexer_7_out), .out(wrData), .sel(memToReg));  // open: en
  Multiplexer #(.width(32)) multiplexer_7 (
    .in0(MEM_data_mem_out), .in1(bit_extender_3_out), .out(multiplexer_7_out), .sel(comparator_3_eq));  // open: en
  Register #(.width(32)) PIPELINE (
    .D(multiplexer_5_out), .Q({INSTRUCTION_t, RS, RT, ADDRESS_J_t}), .clk(CLOCK));  // open: en, clr
  Multiplexer #(.width(32)) multiplexer_8 (
    .in0(RT_READ_VALUE), .in1(RegFile_read_data_2), .out(rt_dataIn), .sel(rtTmp));  // open: en
  Multiplexer #(.width(5)) multiplexer_9 (.in0(wrReg), .in1({5{1'b1}}), .out(Write_Register), .sel(jal));  // open: en
  Comparator #(.width(5), .mode("unsigned")) comparator_4 (.a(5'b00111), .b(RS), .lt(comparator_4_lt));  // open: gt, eq
  Comparator #(.width(5), .mode("unsigned")) comparator_5 (.a(RS), .b(5'b01100), .lt(comparator_5_lt));  // open: gt, eq
  Comparator #(.width(5), .mode("unsigned")) comparator_6 (.a(5'b00111), .b(RT), .lt(comparator_6_lt));  // open: gt, eq
  Comparator #(.width(5), .mode("unsigned")) comparator_7 (.a(RT), .b(5'b01100), .lt(comparator_7_lt));  // open: gt, eq
  assign bit_extender_4_out = {{16{ADDRESS_J_t[15]}}, ADDRESS_J_t};  // Bit_Extender bit_extender_4
  assign bit_extender_5_out = {{16{1'b0}}, ADDRESS_J_t};  // Bit_Extender bit_extender_5
  Multiplexer #(.width(32)) multiplexer_10 (
    .in0(wrData), .in1(bit_extender_6_out), .out(RD_WRITE_VALUE), .sel(jal));  // open: en
  and and_5 (rsTmp, comparator_4_lt, comparator_5_lt);
  and and_6 (rtTmp, comparator_6_lt, comparator_7_lt);
  Multiplexer #(.width(32)) multiplexer_11 (
    .in0(bit_extender_4_out), .in1(bit_extender_5_out), .out(multiplexer_11_out), .sel(zeroExt));  // open: en
  or or_2 (kill, jump, isBranchTaken);
  control control_1 (
    .INSTRUCTION({INSTRUCTION_t, RS, RT, ADDRESS_J_t}), .aluCtrl(aluCtrl), .jal(jal), .regDest(regDest),
    .aluSrc(aluSrc), .lui(lui), .regWrite(RD_WRITE_ENABLE), .memWr(memWr), .memToReg(memToReg),
    .zeroExt(zeroExt), .beq(beq), .bne(bne), .accessByte(accessByte), .jr(jr), .jump(jump), .shamt(shamt_t));
  Multiplexer #(.width(32)) multiplexer_12 (
    .in0(RS_READ_VALUE), .in1(RegFile_read_data_1), .out(valueForBranch), .sel(rsTmp));  // open: en
  Adder #(.width(24)) adder_3 (.a(FETCH_ADDRESS), .b(24'h100000), .out(adder_3_out));  // open: cin, cout
  Multiplexer #(.width(32)) multiplexer_13 (
    .in0(rt_dataIn), .in1(multiplexer_11_out), .out(multiplexer_13_out), .sel(aluSrc));  // open: en
  Subtractor #(.width(32)) subtractor_1 (.a(valueForBranch), .b(rt_dataIn), .out(subtractor_1_out));  // open: bin, bout
  Subtractor #(.width(24)) subtractor_2 (.a(ADDRESS_J), .b(24'h100000), .out(subtractor_2_out));  // open: bin, bout
  assign bit_extender_6_out = {{8{1'b0}}, adder_3_out};  // Bit_Extender bit_extender_6
  Multiplexer #(.width(32)) multiplexer_14 (
    .in0(valueForBranch), .in1(multiplexer_13_out), .out(multiplexer_14_out), .sel(lui));  // open: en
  Multiplexer #(.width(32)) multiplexer_15 (
    .in0(multiplexer_13_out), .in1(32'h10), .out(multiplexer_15_out), .sel(lui));  // open: en
  assign bit_extender_7_out = {{27{1'b0}}, ADDRESS_J_t[10:6]};  // Bit_Extender bit_extender_7
  Comparator #(.width(32)) comparator_8 (.a(subtractor_1_out), .b({32{1'b0}}), .eq(aluEq));  // open: gt, lt
  Multiplexer #(.width(24)) multiplexer_16 (
    .in0(branchVal), .in1(subtractor_2_out), .out(multiplexer_16_out), .sel(jump));  // open: en
  Multiplexer #(.width(32)) multiplexer_17 (
    .in0(multiplexer_14_out), .in1(rt_dataIn), .out(X), .sel(shamt_t));  // open: en
  Multiplexer #(.width(32)) multiplexer_18 (
    .in0(multiplexer_15_out), .in1(bit_extender_7_out), .out(Y), .sel(shamt_t));  // open: en
  Multiplexer #(.width(24)) multiplexer_19 (
    .in0(multiplexer_16_out), .in1(subtractor_3_out), .out(nextPC), .sel(jr));  // open: en
  Subtractor #(.width(24)) subtractor_3 (
    .a(valueForBranch[23:0]), .b(24'h100000), .out(subtractor_3_out));  // open: bin, bout

  // Other names for the same wires on the sheet: FUNCT[5:0] = ADDRESS_J_t[5:0]; IMMEDIATE[15:0] = ADDRESS_J_t;
  //   INSTRUCTION_t[25:0] = {RS, RT, ADDRESS_J_t}; SHAMT[4:0] = ADDRESS_J_t[10:6]; RD[4:0] = ADDRESS_J_t[15:11];
  //   ADDRESS_J_t[25:16] = {RS, RT}; OPCODE[5:0] = INSTRUCTION_t; PC[23:0] = FETCH_ADDRESS; regWr = RD_WRITE_ENABLE

  // Notes on the sheet:
  //   These are outputs/inputs from run.circ
  //   These are outputs to run.circ
endmodule

module control (
  input  [31:0] INSTRUCTION,
  output regDest,
  output regWrite,
  output aluSrc,
  output [5:0] aluCtrl,
  output lui,
  output memWr,
  output memToReg,
  output zeroExt,
  output beq,
  output bne,
  output accessByte,
  output jr,
  output jump,
  output jal,
  output shamt
);

  wire and_3_out, comparator_1_eq, comparator_3_eq, comparator_4_eq, comparator_5_eq, comparator_6_eq,
       comparator_7_eq, comparator_10_eq, comparator_11_eq, comparator_12_eq, comparator_13_eq,
       comparator_14_eq, comparator_16_eq, comparator_17_eq, comparator_18_eq, comparator_19_eq,
       comparator_20_eq, comparator_21_eq, comparator_22_eq, comparator_23_eq, comparator_24_eq,
       comparator_26_eq, comparator_27_eq, comparator_28_eq, comparator_29_eq, comparator_31_eq,
       comparator_32_eq, comparator_33_eq, comparator_34_eq, or_1_out, or_5_out, or_7_out, or_8_out, or_9_out;
  wire [5:0] multiplexer_2_out, multiplexer_3_out;

  Comparator #(.width(6)) comparator_1 (.a(INSTRUCTION[31:26]), .b({6{1'b0}}), .eq(comparator_1_eq));  // open: gt, lt
  Multiplexer #(.width(6)) multiplexer_1 (
    .in0(multiplexer_2_out), .in1(INSTRUCTION[5:0]), .out(aluCtrl), .sel(comparator_1_eq));  // open: en
  Comparator #(.width(6)) comparator_2 (.a(INSTRUCTION[31:26]), .b(6'b101011), .gt(memWr));  // open: eq, lt
  Comparator #(.width(6)) comparator_3 (.a(INSTRUCTION[31:26]), .b(6'b100000), .eq(comparator_3_eq));  // open: gt, lt
  Comparator #(.width(6)) comparator_4 (.a(INSTRUCTION[31:26]), .b(6'b100100), .eq(comparator_4_eq));  // open: gt, lt
  Comparator #(.width(6)) comparator_5 (.a(INSTRUCTION[31:26]), .b(6'b100011), .eq(comparator_5_eq));  // open: gt, lt
  Comparator #(.width(6)) comparator_6 (.a(INSTRUCTION[31:26]), .b(6'b001101), .eq(comparator_6_eq));  // open: gt, lt
  Comparator #(.width(6)) comparator_7 (.a(INSTRUCTION[31:26]), .b(6'b001100), .eq(comparator_7_eq));  // open: gt, lt
  Comparator #(.width(6)) comparator_8 (.a(INSTRUCTION[31:26]), .b(6'b000100), .eq(beq));  // open: gt, lt
  Comparator #(.width(6)) comparator_9 (.a(INSTRUCTION[31:26]), .b(6'b000101), .eq(bne));  // open: gt, lt
  Comparator #(.width(6)) comparator_10 (.a(INSTRUCTION[31:26]), .b(6'b100000), .eq(comparator_10_eq));  // open: gt, lt
  Comparator #(.width(6)) comparator_11 (.a(INSTRUCTION[31:26]), .b(6'b100100), .eq(comparator_11_eq));  // open: gt, lt
  Comparator #(.width(6)) comparator_12 (.a(INSTRUCTION[31:26]), .b({6{1'b0}}), .eq(comparator_12_eq));  // open: gt, lt
  Comparator #(.width(6)) comparator_13 (.a(INSTRUCTION[5:0]), .b(6'b001000), .eq(comparator_13_eq));  // open: gt, lt
  Comparator #(.width(6)) comparator_14 (.a(INSTRUCTION[31:26]), .b(6'b000010), .eq(comparator_14_eq));  // open: gt, lt
  Comparator #(.width(6)) comparator_15 (.a(INSTRUCTION[31:26]), .b(6'b000011), .eq(jal));  // open: gt, lt
  Comparator #(.width(6)) comparator_16 (.a(INSTRUCTION[5:0]), .b({6{1'b0}}), .eq(comparator_16_eq));  // open: gt, lt
  Comparator #(.width(6)) comparator_17 (.a(INSTRUCTION[5:0]), .b(6'b000010), .eq(comparator_17_eq));  // open: gt, lt
  Comparator #(.width(6)) comparator_18 (.a(INSTRUCTION[5:0]), .b(6'b000011), .eq(comparator_18_eq));  // open: gt, lt
  Comparator #(.width(6)) comparator_19 (.a(INSTRUCTION[31:26]), .b({6{1'b0}}), .eq(comparator_19_eq));  // open: gt, lt
  or or_1 (or_1_out, comparator_16_eq, comparator_17_eq, comparator_18_eq);
  Comparator #(.width(6)) comparator_20 (.a(INSTRUCTION[31:26]), .b(6'b001001), .eq(comparator_20_eq));  // open: gt, lt
  Comparator #(.width(6)) comparator_21 (.a(INSTRUCTION[31:26]), .b(6'b100000), .eq(comparator_21_eq));  // open: gt, lt
  Comparator #(.width(6)) comparator_22 (.a(INSTRUCTION[31:26]), .b(6'b100100), .eq(comparator_22_eq));  // open: gt, lt
  Comparator #(.width(6)) comparator_23 (.a(INSTRUCTION[31:26]), .b(6'b100011), .eq(comparator_23_eq));  // open: gt, lt
  Comparator #(.width(6)) comparator_24 (.a(INSTRUCTION[31:26]), .b(6'b101011), .eq(comparator_24_eq));  // open: gt, lt
  or or_2 (memToReg, comparator_3_eq, comparator_4_eq, comparator_5_eq);
  or or_3 (zeroExt, comparator_6_eq, comparator_7_eq);
  or or_4 (accessByte, comparator_10_eq, comparator_11_eq);
  and and_1 (jr, comparator_12_eq, comparator_13_eq);
  and and_2 (shamt, comparator_19_eq, or_1_out);
  Comparator #(.width(6), .mode("unsigned")) comparator_25 (
    .a(INSTRUCTION[31:26]), .b({6{1'b0}}), .eq(regDest));  // open: gt, lt
  Comparator #(.width(6), .mode("unsigned")) comparator_26 (
    .a(INSTRUCTION[31:26]), .b(6'b000011), .eq(comparator_26_eq));  // open: gt, lt
  Comparator #(.width(6), .mode("unsigned")) comparator_27 (
    .a(INSTRUCTION[31:26]), .b(6'b000010), .eq(comparator_27_eq));  // open: gt, lt
  Comparator #(.width(6), .mode("unsigned")) comparator_28 (
    .a(INSTRUCTION[31:26]), .b({6{1'b0}}), .eq(comparator_28_eq));  // open: gt, lt
  or or_5 (or_5_out, comparator_20_eq, comparator_21_eq, comparator_22_eq, comparator_23_eq, comparator_24_eq);
  or or_6 (jump, comparator_14_eq, jal);
  or or_7 (or_7_out, comparator_28_eq, comparator_27_eq, comparator_26_eq);
  not not_1 (aluSrc, or_7_out);
  Comparator #(.width(6), .mode("unsigned")) comparator_29 (
    .a(INSTRUCTION[31:26]), .b(6'b000010), .eq(comparator_29_eq));  // open: gt, lt
  Comparator #(.width(6)) comparator_30 (.a(INSTRUCTION[31:26]), .b(6'b001111), .eq(lui));  // open: gt, lt
  or or_8 (or_8_out, comparator_29_eq, and_3_out, or_9_out);
  not not_2 (regWrite, or_8_out);
  Multiplexer #(.width(6)) multiplexer_2 (
    .in0(multiplexer_3_out), .in1(6'b100001), .out(multiplexer_2_out), .sel(or_5_out));  // open: en
  Multiplexer #(.width(6)) multiplexer_3 (
    .in0(6'b100101), .in1({6{1'b0}}), .out(multiplexer_3_out), .sel(lui));  // open: en
  Comparator #(.width(6), .mode("unsigned")) comparator_31 (
    .a(INSTRUCTION[31:26]), .b({6{1'b0}}), .eq(comparator_31_eq));  // open: gt, lt
  and and_3 (and_3_out, comparator_31_eq, comparator_32_eq);
  or or_9 (or_9_out, comparator_34_eq, comparator_33_eq);
  Comparator #(.width(6), .mode("unsigned")) comparator_32 (
    .a(INSTRUCTION[5:0]), .b(6'b001000), .eq(comparator_32_eq));  // open: gt, lt
  Comparator #(.width(6), .mode("unsigned")) comparator_33 (
    .a(INSTRUCTION[31:26]), .b(6'b000101), .eq(comparator_33_eq));  // open: gt, lt
  Comparator #(.width(6), .mode("unsigned")) comparator_34 (
    .a(INSTRUCTION[31:26]), .b(6'b000100), .eq(comparator_34_eq));  // open: gt, lt

  // Other names for the same wires on the sheet: ADDRESS_J[25:0] = INSTRUCTION[25:0]; FUNCT[5:0] = INSTRUCTION[5:0];
  //   IMMEDIATE[15:0] = INSTRUCTION[15:0]; SHAMT_t[4:0] = INSTRUCTION[10:6]; RD[4:0] = INSTRUCTION[15:11];
  //   RT[4:0] = INSTRUCTION[20:16]; RS[4:0] = INSTRUCTION[25:21]; OPCODE[5:0] = INSTRUCTION[31:26]
endmodule
