// Logisim project regfile.circ as structural Verilog: 1 circuit, main circuit main
module main (
  input  [1:0] Read_register_1,
  input  [1:0] Read_register_2,
  input  [1:0] write_register,
  input  [31:0] write_data,
  input  clock,
  input  RegWrite,
  output [31:0] t0_Value,
  output [31:0] t1_Value,
  output [31:0] t2_Value,
  output [31:0] t3_Value,
  output [31:0] Read_Data_1,
  output [31:0] Read_Data_2
);

  wire en0, en1, en2, en3;
  wire [31:0] _0, _1, _2, _3, controlled_buffer_1_out;

  Demultiplexer #(.select(2), .width(32)) demultiplexer_1 (
    .out0(_0), .out1(_1), .out2(_2), .out3(_3), .in(controlled_buffer_1_out), .sel(write_register));  // open: en
  assign controlled_buffer_1_out = RegWrite ? write_data : 32'bz;  // Controlled_Buffer controlled_buffer_1
  Register #(.width(32)) register_1 (.D(_0), .en(en0), .Q(t0_Value), .clk(clock));  // open: clr
  Demultiplexer #(.select(2)) demultiplexer_2 (
    .out0(en0), .out1(en1), .out2(en2), .out3(en3), .in(1'b1), .sel(write_register));  // open: en
  Register #(.width(32)) register_2 (.D(_1), .en(en1), .Q(t1_Value), .clk(clock));  // open: clr
  Multiplexer #(.select(2), .width(32)) multiplexer_1 (
    .in0(t0_Value), .in1(t1_Value), .in2(t2_Value), .in3(t3_Value), .out(Read_Data_1), .sel(Read_register_1));  // open: en
  Multiplexer #(.select(2), .width(32)) multiplexer_2 (
    .in0(t0_Value), .in1(t1_Value), .in2(t2_Value), .in3(t3_Value), .out(Read_Data_2), .sel(Read_register_2));  // open: en
  Register #(.width(32)) register_3 (.D(_2), .en(en2), .Q(t2_Value), .clk(clock));  // open: clr
  Register #(.width(32)) register_4 (.D(_3), .en(en3), .Q(t3_Value), .clk(clock));  // open: clr

  // Other names for the same wires on the sheet: reg0[31:0] = t0_Value; t0[31:0] = t0_Value; reg1[31:0] = t1_Value;
  //   t1[31:0] = t1_Value; reg2[31:0] = t2_Value; t2[31:0] = t2_Value; reg3[31:0] = t3_Value; t3[31:0] = t3_Value

  // Notes on the sheet:
  //   These are INPUTS to the circuit
  //   These are INPUTS to the circuit
  //   DO NOT CHANGE THE LOCATIONS OF THE INPUTS/OUTPUTS! IF YOU DO SO, YOU NEED TO MAKE SURE THE PINS ARE AT THE RIGHT PLACE!
  //   These are OUTPUTS to the circuit
  //   Yet again, the clock is not an actual clock, but an input, one that will be driven from a higher circuit
  //   These are OUTPUTS to the circuit
endmodule
